// Logisim project Misc-subcircuits.circ as structural Verilog: 1 circuit, main circuit PC_Control
module PC_Control (
  input  [15:0] PC_Branch,
  input  [15:0] PC_Int,
  input  [15:0] PC_C_R,
  input  Branch,
  input  Call,
  input  Interrup,
  output [15:0] PC_out,
  output PC_Change
);

  Multiplexer #(.select(3), .width(16)) multiplexer_1 (
    .in1(PC_Branch), .in2(PC_C_R), .in4(PC_Int), .out(PC_out), .sel({Interrup, Call, Branch}));  // open: in0, in3, in5, in6, in7, en
  or or_1 (PC_Change, Interrup, Call, Branch);

  // Notes on the sheet:
  //   Ideally, execute branch/call first, but interrup will not be true in the next clock cycle...
  //   What do we do if interrupt is triggered while executing a branch/call/return ommand?, e.g.  select bit = 101?
endmodule
