// Logisim project cs356.circ as structural Verilog: 33 circuits, main circuit ROM
module Main (
  input  in_1,
  input  RESET,
  input  in_3,
  input  Clear
);

  wire branch_1_branch, clock_1_out, enable_t2_1_writeenable_yyt2, fpe, in, int_any, k1e, k2e, key_1_enable,
       key_2_enable, key_enable, pc_ctrl_1_pc_change, rete, swi, which_int_1_out_3,
       write_enable_1_writeenable_yyt1;
  wire [3:0] alsu_1_output_2, alsu_1_output_3, call_return_1_a_select, call_return_1_b_select, rselect_A,
       rselect_B, which_int_1_out_4;
  wire [3:3] alsu_1_output;
  wire [4:0] alsu_1_f0__sign;
  wire [6:0] char, keyboard_1_data, keyboard_2_data, printing;
  wire [15:0] branch_1_output, call_return_1_pc__w, call_return_1_ra__w, call_return_1_rb__w, fp1, fp2, i_pc,
       multiplexer_1_out, out_A, out_B, pc_1_current, pc_ctrl_1_pc_out, ra, ram_1_data_from_load, rb,
       rf_1_rfp, swi_pc, wRt;
  wire [15:4] rom_1_output;
  wire [17:0] alsu_1_ram;

  or or_1 (int_any, in, swi);
  BRANCH branch_1 (
    .Flags(alsu_1_f0__sign), .Input_B(out_B), .Instruction({rom_1_output, rselect_B}),
    .Output(branch_1_output), .Branch(branch_1_branch), .Current(pc_1_current));
  CALL_RETURN call_return_1 (
    .Instruction({rom_1_output, rselect_B}), .Input_A(out_A), .Input_B(out_B), .PC(pc_1_current),
    .FP(rf_1_rfp), .Branch(fpe), .FP__w(fp1), .PC__w(call_return_1_pc__w), .Rb__w(call_return_1_rb__w),
    .Ra__w(call_return_1_ra__w), .b_select(call_return_1_b_select),
    .Rd({alsu_1_output_3, alsu_1_output_2, alsu_1_output[3], printing}), .a_select(call_return_1_a_select));
  Hardware_Interrupt hardware_interrupt_1 (
    .Instruction({rom_1_output, rselect_B}), .Input_A(out_A), .PC(pc_1_current),
    .WHich_interupt(which_int_1_out_4), .toggle_interupt(in), .FP__w(fp2), .PC__w(i_pc), .clock(clock_1_out),
    .key_in_board(which_int_1_out_3));
  which_int which_int_1 (.in_1(k1e), .in_2(k2e), .out_3(which_int_1_out_3), .out_4(which_int_1_out_4));
  Software_Interrupt software_interrupt_1 (
    .Instruction({rom_1_output, rselect_B}), .Input_A(out_A), .PC(pc_1_current), .clock(clock_1_out),
    .toggle_interupt(swi), .FP__w(fp2), .PC__w(swi_pc));
  PC_Ctrl pc_ctrl_1 (
    .PC_Branch(branch_1_output), .PC_Int(i_pc), .PC_C_R(call_return_1_pc__w), .PC_SWI(swi_pc),
    .Branch(branch_1_branch), .Call(fpe), .HW_Interrupt(fpe), .SW_Int(swi), .PC_Change(pc_ctrl_1_pc_change),
    .CLK(clock_1_out), .PC_out(pc_ctrl_1_pc_out));
  PC pc_1 (
    .Current(pc_1_current), .Input(pc_ctrl_1_pc_out), .CLK(clock_1_out), .RESET(RESET),
    .Branch(pc_ctrl_1_pc_change));
  Clock clock_1 (.out(clock_1_out));
  Multiplexer #(.width(16), .enable("false")) multiplexer_1 (
    .in0(fp1), .in1(fp2), .out(multiplexer_1_out), .sel(int_any));
  Hex_Digit_Display hex_digit_display_1 (.value(rom_1_output[15:12]));  // open: dp
  ROM rom_1 (.Input(pc_1_current), .Output({rom_1_output, rselect_B}));
  Multiplexer #(.width(16), .enable("false")) multiplexer_2 (
    .in0(call_return_1_ra__w), .out(ra), .sel(in));  // open: in1
  Multiplexer #(.width(16), .enable("false")) multiplexer_3 (
    .in0(call_return_1_rb__w), .out(rb), .sel(in));  // open: in1
  Hex_Digit_Display hex_digit_display_2 (.value(rom_1_output[7:4]));  // open: dp
  Hex_Digit_Display hex_digit_display_3 (.value(rom_1_output[11:8]));  // open: dp
  Miscellaneous__rselectA_MULT miscellaneous_rselecta_mult_1 (
    .Instruction({rom_1_output, rselect_B}), .enable_Rt(rete), .rselectA(rselect_A));
  Hex_Digit_Display hex_digit_display_4 (.value(out_A[15:12]));  // open: dp
  RF rf_1 (
    .Output_A(out_A), .rselect_A(rselect_A), .CLK(clock_1_out), .Output_B(out_B), .rselect_B(rselect_B),
    .rFP(rf_1_rfp), .InputA(ra), .wselectA(call_return_1_a_select), .InputB(rb),
    .wselectB(call_return_1_b_select), .enable_Rt(rete), .wFP(multiplexer_1_out), .enable_FP(fpe), .wRt(wRt),
    .Clear(Clear), .ASCII_char(char), .Keyboard_enabled(key_enable), .enable_interpRt(int_any));
  Hex_Digit_Display hex_digit_display_5 (.value(rselect_B));  // open: dp
  Hex_Digit_Display hex_digit_display_6 (.value(out_A[11:8]));  // open: dp
  Hex_Digit_Display hex_digit_display_7 (.value(out_A[7:4]));  // open: dp
  Hex_Digit_Display hex_digit_display_8 (.value(out_A[3:0]));  // open: dp
  Hex_Digit_Display hex_digit_display_9 (.value(alsu_1_output_3));  // open: dp
  Hex_Digit_Display hex_digit_display_10 (.value(alsu_1_output_2));  // open: dp
  Hex_Digit_Display hex_digit_display_11 (.value(out_B[15:12]));  // open: dp
  Hex_Digit_Display hex_digit_display_12 (.value(out_B[11:8]));  // open: dp
  Hex_Digit_Display hex_digit_display_13 (.value({alsu_1_output[3], printing[6:4]}));  // open: dp
  Hex_Digit_Display hex_digit_display_14 (.value(out_B[7:4]));  // open: dp
  RAM ram_1 (
    .address(alsu_1_ram[15:0]), .CLK(clock_1_out), .Load(alsu_1_ram[16]),
    .data_from_load(ram_1_data_from_load),
    .data_to_store({alsu_1_output_3, alsu_1_output_2, alsu_1_output[3], printing}), .Enable(alsu_1_ram[17]));
  Hex_Digit_Display hex_digit_display_15 (.value(printing[3:0]));  // open: dp
  Hex_Digit_Display hex_digit_display_16 (.value(out_B[3:0]));  // open: dp
  ALSU alsu_1 (
    .Input_A(out_A), .Input_B(out_B), .INSTRUCTION({rom_1_output, rselect_B}), .R13(wRt),
    .F0__sign(alsu_1_f0__sign[0]), .F1__zero(alsu_1_f0__sign[1]), .F2__overflow(alsu_1_f0__sign[2]),
    .F3__carry(alsu_1_f0__sign[3]), .F4__carry_block(alsu_1_f0__sign[4]), .CLK(clock_1_out),
    .Output({alsu_1_output_3, alsu_1_output_2, alsu_1_output[3], printing}),
    .RAM_input(ram_1_data_from_load), .RAM(alsu_1_ram));
  TTY tty_1 (.data(printing), .clk(clock_1_out), .we(write_enable_1_writeenable_yyt1), .clr(in_1));
  Keyboard keyboard_1 (.clk(clock_1_out), .re(key_1_enable), .avail(k1e), .data(keyboard_1_data));  // open: clr
  Write_Enable write_enable_1 (
    .Instruction({rom_1_output, rselect_B}), .WriteEnable_YYT1(write_enable_1_writeenable_yyt1));
  key0 key0_1 (.in_1(k1e), .KeyBoardEnable_YYT1(key_1_enable), .Instruction({rom_1_output, rselect_B}));
  LED F0__sign (.in(alsu_1_f0__sign[0]));
  LED F1__zero (.in(alsu_1_f0__sign[1]));
  LED F2__overflow (.in(alsu_1_f0__sign[2]));
  LED F3__carry (.in(alsu_1_f0__sign[3]));
  LED F4__carry_block (.in(alsu_1_f0__sign[4]));
  Keyboard #(.buflen(256)) keyboard_2 (
    .clk(clock_1_out), .re(key_2_enable), .avail(k2e), .data(keyboard_2_data));  // open: clr
  key2 key2_1 (.Instruction({rom_1_output, rselect_B}), .in_1(k2e), .KeyBoardEnable_YYT1(key_2_enable));
  TTY tty_2 (.data(printing), .clk(clock_1_out), .we(enable_t2_1_writeenable_yyt2), .clr(in_3));
  enable_t2 enable_t2_1 (.Instruction({rom_1_output, rselect_B}), .WriteEnable_YYt2(enable_t2_1_writeenable_yyt2));
  Multiplexer #(.width(7), .enable("false")) multiplexer_4 (
    .in0(keyboard_1_data), .in1(keyboard_2_data), .out(char), .sel(key_2_enable));
  or or_2 (key_enable, key_1_enable, key_2_enable);

  // Notes on the sheet:
  //   Instruction
  //   data from Ra
  //   data to write to Rd
  //   data from Rb
  //   MULT b31-16
endmodule

module Flag (
  input  in_1,
  input  in_2,
  input  CLK,
  input  in_4,
  input  in_5,
  input  in_6,
  output F0__sign,
  output F1__zero,
  output F2__overflow,
  output F3__carry,
  output F4__carry_block
);

  Register #(.width(1)) F0 (.D(in_1), .Q(F0__sign), .clk(CLK));  // open: en, clr
  Register #(.width(1)) F1 (.D(in_2), .Q(F1__zero), .clk(CLK));  // open: en, clr
  Register #(.width(1)) F2 (.D(in_4), .Q(F2__overflow), .clk(CLK));  // open: en, clr
  Register #(.width(1)) F3 (.D(in_5), .Q(F3__carry), .clk(CLK));  // open: en, clr
  Register #(.width(1)) F4 (.D(in_6), .Q(F4__carry_block), .clk(CLK));  // open: en, clr
endmodule

module RF (
  input  Clear,
  input  [15:0] InputA,
  input  [3:0] rselect_A,
  input  [3:0] wselectA,
  input  CLK,
  input  [15:0] InputB,
  input  [3:0] wselectB,
  input  [3:0] rselect_B,
  input  [15:0] wRt,
  input  enable_Rt,
  input  [15:0] wFP,
  input  enable_FP,
  input  [6:0] ASCII_char,
  input  Keyboard_enabled,
  input  enable_interpRt,
  output [15:0] Output_A,
  output [15:0] Output_B,
  output [15:0] rFP
);

  wire decoder_1_out1, decoder_1_out2, decoder_1_out3, decoder_1_out4, decoder_1_out5, decoder_1_out6,
       decoder_1_out7, decoder_1_out8, decoder_1_out9, decoder_1_out10, decoder_1_out11, decoder_1_out12,
       decoder_1_out13, decoder_1_out14, decoder_1_out15, decoder_2_out1, decoder_2_out2, decoder_2_out3,
       decoder_2_out4, decoder_2_out5, decoder_2_out6, decoder_2_out7, decoder_2_out8, decoder_2_out9,
       decoder_2_out10, decoder_2_out11, decoder_2_out12, decoder_2_out13, decoder_2_out14, decoder_2_out15,
       or_1_out, or_2_out, or_3_out, or_4_out, or_5_out, or_6_out, or_7_out, or_8_out, or_9_out, or_10_out,
       or_11_out, or_12_out, or_13_out, or_15_out, or_17_out, or_18_out;
  wire [15:0] _10, bit_extender_1_out, demultiplexer_1_out1, demultiplexer_1_out2, demultiplexer_1_out3,
       demultiplexer_1_out4, demultiplexer_1_out5, demultiplexer_1_out6, demultiplexer_1_out7,
       demultiplexer_1_out8, demultiplexer_1_out9, demultiplexer_1_out10, demultiplexer_1_out11,
       demultiplexer_1_out12, demultiplexer_1_out13, demultiplexer_1_out14, demultiplexer_1_out15,
       demultiplexer_2_out1, demultiplexer_2_out2, demultiplexer_2_out3, demultiplexer_2_out4,
       demultiplexer_2_out5, demultiplexer_2_out6, demultiplexer_2_out7, demultiplexer_2_out8,
       demultiplexer_2_out9, demultiplexer_2_out10, demultiplexer_2_out11, demultiplexer_2_out12,
       demultiplexer_2_out13, demultiplexer_2_out14, demultiplexer_2_out15, multiplexer_2_out,
       multiplexer_3_out, multiplexer_4_out, multiplexer_5_out, multiplexer_6_out, multiplexer_7_out,
       multiplexer_8_out, multiplexer_9_out, multiplexer_10_out, multiplexer_12_out, multiplexer_13_out,
       multiplexer_14_out, multiplexer_15_out, multiplexer_16_out, or_14_out, or_16_out, R0_q, R1_q, R2_q,
       R3_q, R4_q, R5_q, R6_q, R7_q, R8_q, R9_q, R10_q, R11_q, R12_q, R13_q, R15_q, reg_10;

  Decoder #(.select(4)) decoder_1 (
    .out1(decoder_1_out1), .out2(decoder_1_out2), .out3(decoder_1_out3), .out4(decoder_1_out4),
    .out5(decoder_1_out5), .out6(decoder_1_out6), .out7(decoder_1_out7), .out8(decoder_1_out8),
    .out9(decoder_1_out9), .out10(decoder_1_out10), .out11(decoder_1_out11), .out12(decoder_1_out12),
    .out13(decoder_1_out13), .out14(decoder_1_out14), .out15(decoder_1_out15), .sel(wselectA));  // open: out0, en
  Decoder #(.select(4)) decoder_2 (
    .out1(decoder_2_out1), .out2(decoder_2_out2), .out3(decoder_2_out3), .out4(decoder_2_out4),
    .out5(decoder_2_out5), .out6(decoder_2_out6), .out7(decoder_2_out7), .out8(decoder_2_out8),
    .out9(decoder_2_out9), .out10(decoder_2_out10), .out11(decoder_2_out11), .out12(decoder_2_out12),
    .out13(decoder_2_out13), .out14(decoder_2_out14), .out15(decoder_2_out15), .sel(wselectB));  // open: out0, en
  assign bit_extender_1_out = {{9{1'b0}}, ASCII_char};  // Bit_Extender bit_extender_1
  Demultiplexer #(.select(4), .width(16)) demultiplexer_1 (
    .out1(demultiplexer_1_out1), .out2(demultiplexer_1_out2), .out3(demultiplexer_1_out3),
    .out4(demultiplexer_1_out4), .out5(demultiplexer_1_out5), .out6(demultiplexer_1_out6),
    .out7(demultiplexer_1_out7), .out8(demultiplexer_1_out8), .out9(demultiplexer_1_out9),
    .out10(demultiplexer_1_out10), .out11(demultiplexer_1_out11), .out12(demultiplexer_1_out12),
    .out13(demultiplexer_1_out13), .out14(demultiplexer_1_out14), .out15(demultiplexer_1_out15), .in(InputA),
    .sel(wselectA));  // open: out0, en
  Demultiplexer #(.select(4), .width(16)) demultiplexer_2 (
    .out1(demultiplexer_2_out1), .out2(demultiplexer_2_out2), .out3(demultiplexer_2_out3),
    .out4(demultiplexer_2_out4), .out5(demultiplexer_2_out5), .out6(demultiplexer_2_out6),
    .out7(demultiplexer_2_out7), .out8(demultiplexer_2_out8), .out9(demultiplexer_2_out9),
    .out10(demultiplexer_2_out10), .out11(demultiplexer_2_out11), .out12(demultiplexer_2_out12),
    .out13(demultiplexer_2_out13), .out14(demultiplexer_2_out14), .out15(demultiplexer_2_out15), .in(InputB),
    .sel(wselectB));  // open: out0, en
  Multiplexer #(.width(16), .enable("false")) multiplexer_1 (
    .in0(reg_10), .in1(bit_extender_1_out), .out(_10), .sel(Keyboard_enabled));
  or or_1 (or_1_out, enable_Rt, enable_interpRt);
  Multiplexer #(.width(16)) multiplexer_2 (
    .in0(demultiplexer_2_out1), .in1(demultiplexer_1_out1), .out(multiplexer_2_out), .sel(decoder_1_out1));  // open: en
  Multiplexer #(.width(16)) multiplexer_3 (
    .in0(demultiplexer_2_out2), .in1(demultiplexer_1_out2), .out(multiplexer_3_out), .sel(decoder_1_out2));  // open: en
  Multiplexer #(.width(16)) multiplexer_4 (
    .in0(demultiplexer_2_out3), .in1(demultiplexer_1_out3), .out(multiplexer_4_out), .sel(decoder_1_out3));  // open: en
  Multiplexer #(.width(16)) multiplexer_5 (
    .in0(demultiplexer_2_out4), .in1(demultiplexer_1_out4), .out(multiplexer_5_out), .sel(decoder_1_out4));  // open: en
  Multiplexer #(.width(16)) multiplexer_6 (
    .in0(demultiplexer_2_out5), .in1(demultiplexer_1_out5), .out(multiplexer_6_out), .sel(decoder_1_out5));  // open: en
  Multiplexer #(.width(16)) multiplexer_7 (
    .in0(demultiplexer_2_out6), .in1(demultiplexer_1_out6), .out(multiplexer_7_out), .sel(decoder_1_out6));  // open: en
  Multiplexer #(.width(16)) multiplexer_8 (
    .in0(demultiplexer_2_out7), .in1(demultiplexer_1_out7), .out(multiplexer_8_out), .sel(decoder_1_out7));  // open: en
  Multiplexer #(.width(16)) multiplexer_9 (
    .in0(demultiplexer_2_out8), .in1(demultiplexer_1_out8), .out(multiplexer_9_out), .sel(decoder_1_out8));  // open: en
  Multiplexer #(.width(16)) multiplexer_10 (
    .in0(demultiplexer_2_out9), .in1(demultiplexer_1_out9), .out(multiplexer_10_out), .sel(decoder_1_out9));  // open: en
  Multiplexer #(.width(16)) multiplexer_11 (
    .in0(demultiplexer_2_out10), .in1(demultiplexer_1_out10), .out(reg_10), .sel(decoder_1_out10));  // open: en
  Multiplexer #(.width(16)) multiplexer_12 (
    .in0(demultiplexer_2_out11), .in1(demultiplexer_1_out11), .out(multiplexer_12_out), .sel(decoder_1_out11));  // open: en
  Multiplexer #(.width(16)) multiplexer_13 (
    .in0(demultiplexer_2_out12), .in1(demultiplexer_1_out12), .out(multiplexer_13_out), .sel(decoder_1_out12));  // open: en
  Multiplexer #(.width(16)) multiplexer_14 (
    .in0(demultiplexer_2_out13), .in1(demultiplexer_1_out13), .out(multiplexer_14_out), .sel(decoder_1_out13));  // open: en
  Multiplexer #(.width(16)) multiplexer_15 (
    .in0(demultiplexer_2_out14), .in1(demultiplexer_1_out14), .out(multiplexer_15_out), .sel(decoder_1_out14));  // open: en
  Multiplexer #(.width(16)) multiplexer_16 (
    .in0(demultiplexer_2_out15), .in1(demultiplexer_1_out15), .out(multiplexer_16_out), .sel(decoder_1_out15));  // open: en
  Register #(.width(16)) R0 (.D({16{1'b0}}), .Q(R0_q), .clk(CLK), .clr(Clear));  // open: en
  Register #(.width(16)) R1 (.D(multiplexer_2_out), .en(or_2_out), .Q(R1_q), .clk(CLK), .clr(Clear));
  or or_2 (or_2_out, decoder_1_out1, decoder_2_out1);
  Register #(.width(16)) R2 (.D(multiplexer_3_out), .en(or_3_out), .Q(R2_q), .clk(CLK), .clr(Clear));
  or or_3 (or_3_out, decoder_1_out2, decoder_2_out2);
  Register #(.width(16)) R3 (.D(multiplexer_4_out), .en(or_4_out), .Q(R3_q), .clk(CLK), .clr(Clear));
  or or_4 (or_4_out, decoder_1_out3, decoder_2_out3);
  Register #(.width(16)) R4 (.D(multiplexer_5_out), .en(or_5_out), .Q(R4_q), .clk(CLK), .clr(Clear));
  or or_5 (or_5_out, decoder_1_out4, decoder_2_out4);
  Register #(.width(16)) R5 (.D(multiplexer_6_out), .en(or_6_out), .Q(R5_q), .clk(CLK), .clr(Clear));
  or or_6 (or_6_out, decoder_1_out5, decoder_2_out5);
  Register #(.width(16)) R6 (.D(multiplexer_7_out), .en(or_7_out), .Q(R6_q), .clk(CLK), .clr(Clear));
  or or_7 (or_7_out, decoder_1_out6, decoder_2_out6);
  Register #(.width(16)) R7 (.D(multiplexer_8_out), .en(or_8_out), .Q(R7_q), .clk(CLK), .clr(Clear));
  or or_8 (or_8_out, decoder_1_out7, decoder_2_out7);
  Register #(.width(16)) R8 (.D(multiplexer_9_out), .en(or_9_out), .Q(R8_q), .clk(CLK), .clr(Clear));
  or or_9 (or_9_out, decoder_1_out8, decoder_2_out8);
  Register #(.width(16)) R9 (.D(multiplexer_10_out), .en(or_10_out), .Q(R9_q), .clk(CLK), .clr(Clear));
  or or_10 (or_10_out, decoder_1_out9, decoder_2_out9);
  Register #(.width(16)) R10 (.D(_10), .en(or_11_out), .Q(R10_q), .clk(CLK), .clr(Clear));
  or or_11 (or_11_out, decoder_1_out10, decoder_2_out10);
  Register #(.width(16)) R11 (.D(multiplexer_12_out), .en(or_12_out), .Q(R11_q), .clk(CLK), .clr(Clear));
  or or_12 (or_12_out, decoder_1_out11, decoder_2_out11);
  Register #(.width(16)) R12 (.D(multiplexer_13_out), .en(or_13_out), .Q(R12_q), .clk(CLK), .clr(Clear));
  or or_13 (or_13_out, decoder_1_out12, decoder_2_out12);
  Register #(.width(16)) R13 (.D(or_14_out), .en(or_15_out), .Q(R13_q), .clk(CLK), .clr(Clear));
  assign or_14_out = multiplexer_14_out | wRt;  // OR_Gate or_14, 16 bits wide
  or or_15 (or_15_out, or_1_out, decoder_1_out13, decoder_2_out13);
  Register #(.width(16)) R14 (.D(or_16_out), .en(or_17_out), .Q(rFP), .clk(CLK), .clr(Clear));
  assign or_16_out = multiplexer_15_out | wFP;  // OR_Gate or_16, 16 bits wide
  or or_17 (or_17_out, enable_FP, decoder_1_out14, decoder_2_out14);
  Register #(.width(16)) R15 (.D(multiplexer_16_out), .en(or_18_out), .Q(R15_q), .clk(CLK), .clr(Clear));
  or or_18 (or_18_out, decoder_1_out15, decoder_2_out15);
  Multiplexer #(.select(4), .width(16)) multiplexer_17 (
    .in0(R0_q), .in1(R1_q), .in2(R2_q), .in3(R3_q), .in4(R4_q), .in5(R5_q), .in6(R6_q), .in7(R7_q),
    .in8(R8_q), .in9(R9_q), .in10(R10_q), .in11(R11_q), .in12(R12_q), .in13(R13_q), .in14(rFP), .in15(R15_q),
    .out(Output_A), .sel(rselect_A));  // open: en
  Multiplexer #(.select(4), .width(16)) multiplexer_18 (
    .in0(R0_q), .in1(R1_q), .in2(R2_q), .in3(R3_q), .in4(R4_q), .in5(R5_q), .in6(R6_q), .in7(R7_q),
    .in8(R8_q), .in9(R9_q), .in10(R10_q), .in11(R11_q), .in12(R12_q), .in13(R13_q), .in14(rFP), .in15(R15_q),
    .out(Output_B), .sel(rselect_B));  // open: en
endmodule

module PC (
  input  [15:0] Input,
  input  RESET,
  input  CLK,
  input  Branch,
  output [15:0] Current
);

  wire not_1_out;

  not not_1 (not_1_out, Branch);
  Counter #(.width(16), .max('hffff)) counter_1 (
    .load(Branch), .D(Input), .count(not_1_out), .Q(Current), .clk(CLK), .clr(RESET));  // open: carry
endmodule

module ROM (
  input  [15:0] Input,
  output [15:0] Output
);

  ROM_part #(.addrWidth(16), .dataWidth(16)) rom_1 (.addr(Input), .data(Output));  // open: sel

  // Notes on the sheet:
  //   Instruction Memory
  //   contents of rom_1 (hex, n*v repeats v):
  //   2201 2202 100b 32765*0 7100 7210 7320 7430 7540 7650 7760 7870 7980 7a90 7bb0 7cb0 7dc0 7ed0 7fe0
  //   3170 71f0 41f0 3178 4100 4210 4320 4430 4540 4650 4760 4870 4980 4a90 4ba0 4cb0 4dc0 4ed0 4fe0 3180
  //   3380 3580 3780 3980 fb 4056*0 6100 6210 6320 6430 6540 6650 6760 6870 6980 6a90 6ba0 6cb0 6dc0 6ed0
  //   6fe0 3170 61f0 51f0 3178 5100 5210 5320 5430 5540 5650 5760 5870 5980 5a90 5ba0 5cb0 5dc0 5ed0 5fe0
  //   3280 3480 3680 3880 3a80 fb 11144*0 6100 6210 6320 6430 6540 6650 6760 6870 6980 6a90 6ba0 6cb0 6dc0
  //   6ed0 6fe0 3170 61f0 2a00 91a0 a001 41f0 3178 4100 4210 4320 4430 4540 4650 4760 4870 4980 4a90 4ba0
  //   4cb0 4dc0 4ed0 4fe0 2300 42*0 6100 6210 6320 6430 6540 6650 6760 6870 6980 6a90 6ba0 6cb0 6dc0 6ed0
  //   6fe0 3170 61f0 3160 ea00 2a01 e100 f140 4401 3480 6401 a114 6a01 e30a 3068 b0a3 802 e e100 f140 6001
  //   e101 f140 4201 a002 6001 3068 b023 803 3180 f9 41f0 3178 4100 4210 4320 4430 4540 4650 4760 4870
  //   4980 4a90 4ba0 4cb0 4dc0 4ed0 4fe0 2300 17249*0 2300
endmodule

module RAM (
  input  [15:0] address,
  input  [15:0] data_to_store,
  input  CLK,
  input  Load,
  input  Enable,
  output [15:0] data_from_load
);

  wire not_1_out, reset_out;

  Button reset (.out(reset_out));
  RAM_part #(.addrWidth(16), .dataWidth(16)) ram_1 (
    .addr(address), .data(data_from_load), .sel(Enable), .clk(CLK), .ld(Load), .clr(reset_out));
  assign data_from_load = not_1_out ? data_to_store : 16'bz;  // Controlled_Buffer controlled_buffer_1
  not not_1 (not_1_out, Load);
endmodule

// BR
module BRANCH (
  input  [15:0] Instruction,
  input  [4:0] Flags,
  input  [15:0] Current,
  input  [15:0] Input_B,
  output Branch,
  output [15:0] Output
);

  wire comparator_1_lt, multiplexer_2_out, nor_1_out, nor_2_out, not_1_out, not_2_out, not_3_out, not_4_out,
       or_1_out, or_2_out, xnor_1_out, xor_1_out, xor_2_out, xor_3_out;
  wire [15:0] adder_1_out, bit_extender_1_out;

  assign bit_extender_1_out = {{8{Instruction[7]}}, Instruction[7:0]};  // Bit_Extender bit_extender_1
  Adder #(.width(16)) adder_1 (.a(bit_extender_1_out), .b(Current), .out(adder_1_out));  // open: cin, cout
  Multiplexer #(.width(16)) multiplexer_1 (
    .in0(adder_1_out), .in1(Input_B), .out(Output), .sel(Instruction[12]));  // open: en
  Comparator #(.width(4), .mode("unsigned")) comparator_1 (
    .a(Instruction[15:12]), .b(4'b0010), .lt(comparator_1_lt));  // open: gt, eq
  xor xor_1 (xor_1_out, Flags[0], Flags[2]);
  xnor xnor_1 (xnor_1_out, Flags[0], Flags[2]);
  xor xor_2 (xor_2_out, Flags[0], Flags[2]);
  xor xor_3 (xor_3_out, Flags[0], Flags[2]);
  or or_1 (or_1_out, ~Flags[3], Flags[1]);  // OR_Gate
  not not_1 (not_1_out, Flags[1]);
  not not_2 (not_2_out, Flags[3]);
  not not_3 (not_3_out, Flags[0]);
  not not_4 (not_4_out, Flags[2]);
  or or_2 (or_2_out, Flags[2], xor_2_out);
  nor nor_1 (nor_1_out, Flags[1], xor_3_out);
  nor nor_2 (nor_2_out, ~Flags[3], Flags[1]);  // NOR_Gate
  Multiplexer #(.select(4)) multiplexer_2 (
    .in0(1'b1), .in1(1'b0), .in2(xor_1_out), .in3(xnor_1_out), .in4(or_2_out), .in5(nor_1_out),
    .in6(or_1_out), .in7(nor_2_out), .in8(Flags[1]), .in9(not_1_out), .in10(Flags[3]), .in11(not_2_out),
    .in12(Flags[0]), .in13(not_3_out), .in14(Flags[2]), .in15(not_4_out), .out(multiplexer_2_out),
    .sel(Instruction[11:8]));  // open: en
  and and_1 (Branch, comparator_1_lt, multiplexer_2_out);
endmodule

module CALL_RETURN (
  input  [15:0] Instruction,
  input  [15:0] Input_A,
  input  [15:0] Input_B,
  input  [15:0] PC,
  input  [15:0] Rd,
  input  [15:0] FP,
  output Branch,
  output [3:0] b_select,
  output [3:0] a_select,
  output [15:0] FP__w,
  output [15:0] PC__w,
  output [15:0] Rb__w,
  output [15:0] Ra__w
);

  wire and_1_out, and_2_out, and_3_out, comparator_1_eq, comparator_2_eq, decoder_1_out0, decoder_1_out1;
  wire [3:0] multiplexer_2_out;
  wire [15:0] adder_1_out, multiplexer_5_out;

  Decoder #(.select(4)) decoder_1 (
    .out0(decoder_1_out0), .out1(decoder_1_out1), .sel(Instruction[11:8]));  // open: out2, out3, out4, out5, out6, out7, out8, out9, out10, out11, out12, out13, out14, out15, en
  Comparator #(.width(4)) comparator_1 (.a(Instruction[15:12]), .b(4'b0010), .eq(comparator_1_eq));  // open: gt, lt
  Comparator #(.width(4)) comparator_2 (.a(Instruction[11:8]), .b(4'b0011), .eq(comparator_2_eq));  // open: gt, lt
  Multiplexer #(.width(4)) multiplexer_1 (
    .in0(4'b0000), .in1(Instruction[3:0]), .out(b_select), .sel(Branch));  // open: en
  Adder #(.width(16)) adder_1 (.a(PC), .b(16'h1), .out(adder_1_out));  // open: cin, cout
  and and_1 (and_1_out, comparator_2_eq, comparator_1_eq);
  Multiplexer #(.width(4)) multiplexer_2 (
    .in0(Instruction[11:8]), .out(multiplexer_2_out), .sel(and_1_out));  // open: in1, en
  and and_2 (and_2_out, decoder_1_out0, comparator_1_eq);
  and and_3 (and_3_out, decoder_1_out1, comparator_1_eq);
  Multiplexer #(.width(4)) multiplexer_3 (
    .in0(multiplexer_2_out), .in1(Instruction[7:4]), .out(a_select), .sel(Branch));  // open: en
  or or_1 (Branch, and_2_out, and_3_out);
  Multiplexer #(.width(16)) multiplexer_4 (.in1(multiplexer_5_out), .out(Rb__w), .sel(Branch));  // open: in0, en
  Multiplexer #(.width(16)) multiplexer_5 (
    .in1(adder_1_out), .out(multiplexer_5_out), .sel(and_2_out));  // open: in0, en
  Multiplexer #(.width(16)) multiplexer_6 (.in0(Rd), .in1(FP), .out(Ra__w), .sel(Branch));  // open: en

  assign FP__w = Input_A;
  assign PC__w = Input_B;
endmodule

module ALSU (
  input  [15:0] INSTRUCTION,
  input  [15:0] RAM_input,
  input  [15:0] Input_A,
  input  [15:0] Input_B,
  input  CLK,
  output [15:0] R13,
  output [17:0] RAM,
  output [15:0] Output,
  output F0__sign,
  output F1__zero,
  output F2__overflow,
  output F3__carry,
  output F4__carry_block
);

  wire ADD_C_in_out, not_1_out, SUB_C_in_out;
  wire [20:0] add_1_out_4, and_or_xor_1_and, and_or_xor_1_or, and_or_xor_1_xor, dec_1_output, inc_1_output,
       load_store_1_load_2, load_store_1_store, lsl8_1_lsl8, lsl_asl_1_asl, lsl_asl_1_lsl, lsr8_1_lsl8,
       lsr_asr_1_asr, lsr_asr_1_lsr, mult_1_main_result, multiplexer_1_out, multiplexer_2_out,
       set_clrf_save_rstrf_1_restoref, set_clrf_save_rstrf_1_savef, set_clrf_save_rstrf_1_set_clrf,
       sethi_1_output, setlo_1_output, sub_1_out_4;
  wire [20:16] multiplexer_3_out;

  Hex_Digit_Display hex_digit_display_1 (.value(Input_A[15:12]));  // open: dp
  Hex_Digit_Display hex_digit_display_2 (.value(Input_B[15:12]));  // open: dp
  Hex_Digit_Display hex_digit_display_3 (.value(Input_A[11:8]));  // open: dp
  Hex_Digit_Display hex_digit_display_4 (.value(Input_B[11:8]));  // open: dp
  Hex_Digit_Display hex_digit_display_5 (.value(Input_A[7:4]));  // open: dp
  Hex_Digit_Display hex_digit_display_6 (.value(Input_A[3:0]));  // open: dp
  Hex_Digit_Display hex_digit_display_7 (.value(Input_B[7:4]));  // open: dp
  Hex_Digit_Display hex_digit_display_8 (.value(Input_B[3:0]));  // open: dp
  not not_1 (not_1_out, INSTRUCTION[13]);
  LOAD_STORE load_store_1 (
    .offset({INSTRUCTION[12], INSTRUCTION[7:4]}), .Input_B(Input_B), .LOAD_2(load_store_1_load_2),
    .Load(not_1_out), .Input_A__Rd(Input_A), .STORE(load_store_1_store), .b15_12(INSTRUCTION[15:12]),
    .RAM_input(RAM_input), .RAM(RAM));
  LSL_ASL lsl_asl_1 (.Input_B(Input_B), .C_in(ADD_C_in_out), .LSL(lsl_asl_1_lsl), .ASL(lsl_asl_1_asl));
  LSR_ASR lsr_asr_1 (.Input_B(Input_B), .ASR(lsr_asr_1_asr), .LSR(lsr_asr_1_lsr), .C_in(ADD_C_in_out));
  LSL8 lsl8_1 (.LSL8(lsl8_1_lsl8));  // open: Input_B
  LSR8 lsr8_1 (.Input_B(Input_B), .LSL8(lsr8_1_lsl8));
  INC inc_1 (.Input_A__Rd(Input_A), .Epsilon(INSTRUCTION[5:0]), .OUTPUT(inc_1_output));
  DEC dec_1 (.Input_A__Rd(Input_A), .Epsilon(INSTRUCTION[5:0]), .OUTPUT(dec_1_output));
  AND_OR_XOR and_or_xor_1 (
    .Input_A(Input_A), .Input_B(Input_B), .AND(and_or_xor_1_and), .OR(and_or_xor_1_or), .XOR(and_or_xor_1_xor));
  ADD add_1 (.Input_A(Input_A), .Input_B(Input_B), .C_in(ADD_C_in_out), .out_4(add_1_out_4));
  SUB sub_1 (.Input_A(Input_A), .Input_B(Input_B), .C_in(SUB_C_in_out), .out_4(sub_1_out_4));
  MULT mult_1 (.Input_A(Input_A), .Input_B(Input_B), .Main_result(mult_1_main_result), .R13(R13));
  SETLO setlo_1 (.v__b7_0(INSTRUCTION[7:0]), .OUTPUT(setlo_1_output));
  SETHI sethi_1 (.Input_A__Rd(Input_A), .v__b7_0(INSTRUCTION[7:0]), .OUTPUT(sethi_1_output));
  SET_CLRF_SAVE_RSTRF set_clrf_save_rstrf_1 (
    .v0_v4({INSTRUCTION[8], INSTRUCTION[3:0]}), .f0(F0__sign), .f1(F1__zero), .f2(F2__overflow),
    .f3(F3__carry), .f4(F4__carry_block), .b11(INSTRUCTION[11]), .saveF(set_clrf_save_rstrf_1_savef),
    .SET_CLRF(set_clrf_save_rstrf_1_set_clrf), .restoreF(set_clrf_save_rstrf_1_restoref),
    .Input_A__Rd(Input_A));
  Multiplexer #(.width(21), .enable("false")) multiplexer_1 (
    .in0(set_clrf_save_rstrf_1_savef), .in1(set_clrf_save_rstrf_1_restoref), .out(multiplexer_1_out),
    .sel(INSTRUCTION[3]));
  Multiplexer #(.select(4), .width(21)) multiplexer_2 (
    .in0(lsl_asl_1_lsl), .in1(lsr_asr_1_lsr), .in2(lsl8_1_lsl8), .in3(lsr8_1_lsl8), .in4(lsl_asl_1_asl),
    .in5(lsr_asr_1_asr), .in6(set_clrf_save_rstrf_1_set_clrf), .in7(multiplexer_1_out), .in8(inc_1_output),
    .in9(inc_1_output), .in10(inc_1_output), .in11(inc_1_output), .in12(dec_1_output), .in13(dec_1_output),
    .in14(dec_1_output), .in15(dec_1_output), .out(multiplexer_2_out), .sel(INSTRUCTION[7:4]));  // open: en
  Hex_Digit_Display hex_digit_display_9 (.value(INSTRUCTION[15:12]));  // open: dp
  Hex_Digit_Display hex_digit_display_10 (.value(INSTRUCTION[11:8]));  // open: dp
  Multiplexer #(.select(4), .width(21)) multiplexer_3 (
    .in3(multiplexer_2_out), .in4(load_store_1_load_2), .in5(load_store_1_load_2), .in6(load_store_1_store),
    .in7(load_store_1_store), .in8(and_or_xor_1_and), .in9(and_or_xor_1_or), .in10(add_1_out_4),
    .in11(sub_1_out_4), .in12(mult_1_main_result), .in13(and_or_xor_1_xor), .in14(setlo_1_output),
    .in15(sethi_1_output), .out({multiplexer_3_out, Output}), .sel(INSTRUCTION[15:12]));  // open: in0, in1, in2, en
  and SUB_C_in (SUB_C_in_out, ~F4__carry_block, ~F3__carry);  // AND_Gate
  and ADD_C_in (ADD_C_in_out, F3__carry, ~F4__carry_block);  // AND_Gate
  Hex_Digit_Display hex_digit_display_11 (.value(INSTRUCTION[3:0]));  // open: dp
  Hex_Digit_Display hex_digit_display_12 (.value(INSTRUCTION[7:4]));  // open: dp
  Hex_Digit_Display hex_digit_display_13 (.value(Output[15:12]));  // open: dp
  Flag flag_1 (
    .in_1(multiplexer_3_out[16]), .in_2(multiplexer_3_out[17]), .in_4(multiplexer_3_out[18]),
    .in_5(multiplexer_3_out[19]), .in_6(multiplexer_3_out[20]), .F0__sign(F0__sign), .F1__zero(F1__zero),
    .CLK(CLK), .F2__overflow(F2__overflow), .F3__carry(F3__carry), .F4__carry_block(F4__carry_block));
  Hex_Digit_Display hex_digit_display_14 (.value(Output[11:8]));  // open: dp
  Hex_Digit_Display hex_digit_display_15 (.value(Output[7:4]));  // open: dp
  Hex_Digit_Display hex_digit_display_16 (.value(Output[3:0]));  // open: dp

  // Notes on the sheet:
  //   offset value
endmodule

// LD/STR
module LOAD_STORE (
  input  [15:0] RAM_input,
  input  [15:0] Input_A__Rd,
  input  [4:0] offset,
  input  [15:0] Input_B,
  input  Load,
  input  [3:0] b15_12,
  output [20:0] LOAD_2,
  output [17:0] RAM,
  output [20:0] STORE
);

  wire [15:0] bit_extender_1_out;

  assign bit_extender_1_out = {{11{1'b0}}, offset};  // Bit_Extender bit_extender_1
  Comparator #(.width(2), .mode("unsigned")) comparator_1 (.a(2'b01), .b(b15_12[3:2]), .eq(RAM[17]));  // open: gt, lt
  Adder #(.width(16)) adder_1 (.a(bit_extender_1_out), .b(Input_B), .out(RAM[15:0]));  // open: cin, cout
  Comparator #(.width(16)) comparator_2 (.a(RAM_input), .b({16{1'b0}}), .eq(LOAD_2[17]));  // open: gt, lt

  assign LOAD_2[16:0] = {{2{RAM_input[15]}}, RAM_input[14:0]};
  assign RAM[16] = Load;
  assign STORE[15:0] = Input_A__Rd;
endmodule

// A/O/X
module AND_OR_XOR (
  input  [15:0] Input_A,
  input  [15:0] Input_B,
  output [20:0] AND,
  output [20:0] OR,
  output [20:0] XOR
);

  assign {AND[16], AND[14:0]} = Input_A & Input_B;  // AND_Gate and_1, 16 bits wide
  assign {OR[16], OR[14:0]} = Input_A | Input_B;  // OR_Gate or_1, 16 bits wide
  assign {XOR[16], XOR[14:0]} = Input_A ^ Input_B;  // XOR_Gate xor_1, 16 bits wide
  Comparator #(.width(16)) comparator_1 (.a({AND[16], AND[14:0]}), .b({16{1'b0}}), .eq(AND[17]));  // open: gt, lt
  Comparator #(.width(16)) comparator_2 (.a({OR[16], OR[14:0]}), .b({16{1'b0}}), .eq(OR[17]));  // open: gt, lt
  Comparator #(.width(16)) comparator_3 (.a({XOR[16], XOR[14:0]}), .b({16{1'b0}}), .eq(XOR[17]));  // open: gt, lt

  assign AND[15] = AND[16];
  assign OR[15] = OR[16];
  assign XOR[15] = XOR[16];
endmodule

module ADD (
  input  C_in,
  input  [15:0] Input_A,
  input  [15:0] Input_B,
  output [20:0] out_4
);

  wire decoder_1_out1, decoder_1_out4, decoder_1_out6, decoder_1_out7;

  Adder #(.width(16)) adder_1 (.a(Input_A), .b(Input_B), .out(out_4[15:0]), .cin(C_in), .cout(out_4[19]));
  Decoder #(.select(3)) decoder_1 (
    .out1(decoder_1_out1), .out4(decoder_1_out4), .out6(decoder_1_out6), .out7(decoder_1_out7),
    .sel({Input_B[15], Input_A[15], out_4[16]}));  // open: out0, out2, out3, out5, en
  BitSelector #(.width(16)) bitselector_1 (.in(out_4[15:0]), .out(out_4[16]), .sel(4'b1111));
  // OR_Gate sign_bit has open pins: in0=decoder_1_out4, in1=decoder_1_out6, in2=decoder_1_out7, out=open
  Comparator #(.width(16)) comparator_1 (.a(out_4[15:0]), .b({16{1'b0}}), .eq(out_4[17]));  // open: gt, lt
  or overflow (out_4[18], decoder_1_out1, decoder_1_out6);

  // Notes on the sheet:
  //   If both are negative, overflow occurs when the c_out is false
  //   If both are positive, overflow occurs when the c_out true
  //   If one is positive and the other is negative, there can't be overflow
endmodule

module SUB (
  input  C_in,
  input  [15:0] Input_A,
  input  [15:0] Input_B,
  output [20:0] out_4
);

  wire decoder_1_out1, decoder_1_out2, decoder_1_out5, decoder_1_out7, subtractor_1_bout;

  Decoder #(.select(3)) decoder_1 (
    .out1(decoder_1_out1), .out2(decoder_1_out2), .out5(decoder_1_out5), .out7(decoder_1_out7),
    .sel({Input_B[15], Input_A[15], out_4[16]}));  // open: out0, out3, out4, out6, en
  Subtractor #(.width(16)) subtractor_1 (
    .a(Input_A), .b(Input_B), .out(out_4[15:0]), .bin(C_in), .bout(subtractor_1_bout));
  BitSelector #(.width(16)) bitselector_1 (.in(out_4[15:0]), .out(out_4[16]), .sel(4'b1111));
  not not_1 (out_4[19], subtractor_1_bout);
  // OR_Gate sign_bit has open pins: in0=decoder_1_out7, in1=decoder_1_out1, in2=decoder_1_out2, out=open
  Comparator #(.width(16)) comparator_1 (.a(out_4[15:0]), .b({16{1'b0}}), .eq(out_4[17]));  // open: gt, lt
  or overflow (out_4[18], decoder_1_out2, decoder_1_out5);
endmodule

module LSL_ASL (
  input  [15:0] Input_B,
  input  C_in,
  output [20:0] LSL,
  output [20:0] ASL
);

  wire and_1_out, multiplexer_1_out;
  wire [15:0] bit_extender_1_out;
  wire [20:0] add_1_out_4;

  Multiplexer multiplexer_1 (.in1(Input_B[15]), .out(multiplexer_1_out), .sel(C_in));  // open: in0, en
  Shifter #(.width(16)) shifter_1 (.in(Input_B), .\dist (4'b0001), .out({LSL[16], LSL[14:0]}));
  assign bit_extender_1_out = {{15{1'b0}}, and_1_out};  // Bit_Extender bit_extender_1
  and and_1 (and_1_out, multiplexer_1_out, C_in);
  ADD add_1 (.Input_A(Input_B), .Input_B(Input_B), .out_4(add_1_out_4));  // open: C_in
  Adder #(.width(16)) adder_1 (
    .a({LSL[16], LSL[14:0]}), .b(bit_extender_1_out), .out({ASL[16], ASL[14:0]}), .cin(1'b0));  // open: cout
  BitSelector #(.width(21)) bitselector_1 (.in(add_1_out_4), .out(ASL[18]), .sel(5'b10010));
  Comparator #(.width(16)) comparator_1 (.a({LSL[16], LSL[14:0]}), .b({16{1'b0}}), .eq(LSL[17]));  // open: gt, lt
  Comparator #(.width(16)) comparator_2 (.a({ASL[16], ASL[14:0]}), .b({16{1'b0}}), .eq(ASL[17]));  // open: gt, lt

  assign {ASL[19], ASL[15]} = {Input_B[15], ASL[16]};
  assign {LSL[19], LSL[15]} = {Input_B[15], LSL[16]};
endmodule

module LSR_ASR (
  input  [15:0] Input_B,
  input  C_in,
  output [20:0] ASR,
  output [20:0] LSR
);

  Shifter #(.width(16), .shift("ar")) shifter_1 (.in(Input_B), .\dist (4'b0001), .out({ASR[16], ASR[14:0]}));
  Comparator #(.width(16)) comparator_1 (.a({ASR[16], ASR[14:0]}), .b({16{1'b0}}), .eq(ASR[17]));  // open: gt, lt
  Comparator #(.width(16)) comparator_2 (.a({C_in, Input_B[15:1]}), .b({16{1'b0}}), .eq(LSR[17]));  // open: gt, lt

  assign {ASR[19], ASR[15]} = {Input_B[0], ASR[16]};
  assign {LSR[19], LSR[16:0]} = {Input_B[0], {2{C_in}}, Input_B[15:1]};
endmodule

module LSL8 (
  input  [15:0] Input_B,
  output [20:0] LSL8
);

  Shifter #(.width(16)) shifter_1 (.in(Input_B), .\dist (4'b1000), .out({LSL8[16], LSL8[14:0]}));
  Comparator #(.width(16)) comparator_1 (.a({LSL8[16], LSL8[14:0]}), .b({16{1'b0}}), .eq(LSL8[17]));  // open: gt, lt

  assign LSL8[15] = LSL8[16];
endmodule

module LSR8 (
  input  [15:0] Input_B,
  output [20:0] LSL8
);

  Shifter #(.width(16), .shift("lr")) shifter_1 (.in(Input_B), .\dist (4'b1000), .out({LSL8[16], LSL8[14:0]}));
  Comparator #(.width(16)) comparator_1 (.a({LSL8[16], LSL8[14:0]}), .b({16{1'b0}}), .eq(LSL8[17]));  // open: gt, lt

  assign LSL8[15] = LSL8[16];
endmodule

// FLAG OPS
module SET_CLRF_SAVE_RSTRF (
  input  [4:0] v0_v4,
  input  f0,
  input  f1,
  input  b11,
  input  f2,
  input  f3,
  input  f4,
  input  [15:0] Input_A__Rd,
  output [20:0] SET_CLRF,
  output [20:0] saveF,
  output [20:0] restoreF
);

  wire [4:0] and_1_out, or_1_out;

  assign saveF[15:0] = {{11{1'b0}}, {f4, f3, f2, f1, f0}};  // Bit_Extender bit_extender_1
  and and_1 (and_1_out[0], ~v0_v4[0], f0);  // AND_Gate
  and and_2 (and_1_out[1], ~v0_v4[1], f1);  // AND_Gate
  and and_3 (and_1_out[2], ~v0_v4[2], f2);  // AND_Gate
  and and_4 (and_1_out[3], ~v0_v4[3], f3);  // AND_Gate
  and and_5 (and_1_out[4], ~v0_v4[4], f4);  // AND_Gate
  or or_1 (or_1_out[0], v0_v4[0], f0);
  or or_2 (or_1_out[1], v0_v4[1], f1);
  or or_3 (or_1_out[2], v0_v4[2], f2);
  or or_4 (or_1_out[3], v0_v4[3], f3);
  or or_5 (or_1_out[4], v0_v4[4], f4);
  Multiplexer #(.width(5)) multiplexer_1 (
    .in0(or_1_out), .in1(and_1_out), .out(SET_CLRF[20:16]), .sel(b11));  // open: en

  assign restoreF[20:16] = Input_A__Rd[4:0];
endmodule

module INC (
  input  [15:0] Input_A__Rd,
  input  [5:0] Epsilon,
  output [20:0] OUTPUT
);

  wire [14:0] adder_2_out, bit_extender_1_out;

  assign bit_extender_1_out = {{9{1'b0}}, Epsilon};  // Bit_Extender bit_extender_1
  Adder #(.width(15)) adder_1 (
    .a(Input_A__Rd[14:0]), .b(adder_2_out), .out(OUTPUT[14:0]), .cout(OUTPUT[19]));  // open: cin
  Adder #(.width(15)) adder_2 (.a(bit_extender_1_out), .b(15'h1), .out(adder_2_out));  // open: cin, cout
  and and_1 (OUTPUT[16], Input_A__Rd[15], ~OUTPUT[19]);  // AND_Gate
  and and_2 (OUTPUT[18], OUTPUT[19], ~Input_A__Rd[15]);  // AND_Gate
  Comparator #(.width(16)) comparator_1 (
    .a({OUTPUT[16], OUTPUT[14:0]}), .b({16{1'b0}}), .eq(OUTPUT[17]));  // open: gt, lt

  assign OUTPUT[15] = OUTPUT[16];
endmodule

module DEC (
  input  [15:0] Input_A__Rd,
  input  [5:0] Epsilon,
  output [20:0] OUTPUT
);

  wire subtractor_1_bout;
  wire [14:0] adder_1_out, bit_extender_1_out;

  assign bit_extender_1_out = {{9{1'b0}}, Epsilon};  // Bit_Extender bit_extender_1
  Subtractor #(.width(15)) subtractor_1 (
    .a(Input_A__Rd[14:0]), .b(adder_1_out), .out(OUTPUT[14:0]), .bout(subtractor_1_bout));  // open: bin
  Adder #(.width(15)) adder_1 (.a(bit_extender_1_out), .b(15'h1), .out(adder_1_out));  // open: cin, cout
  or or_1 (OUTPUT[16], Input_A__Rd[15], subtractor_1_bout);
  and and_1 (OUTPUT[18], subtractor_1_bout, Input_A__Rd[15]);
  not not_1 (OUTPUT[19], subtractor_1_bout);
  Comparator #(.width(16)) comparator_1 (
    .a({OUTPUT[16], OUTPUT[14:0]}), .b({16{1'b0}}), .eq(OUTPUT[17]));  // open: gt, lt

  assign OUTPUT[15] = OUTPUT[16];
endmodule

module MULT (
  input  [15:0] Input_A,
  input  [15:0] Input_B,
  output [15:0] R13,
  output [20:0] Main_result
);

  wire comparator_2_eq, n2_s_comp_for_mult_4_c_out, xor_1_out;
  wire [15:0] multiplier_1_cout, multiplier_1_out, n2_s_comp_for_mult_1_absolute_value,
       n2_s_comp_for_mult_2_absolute_value;
  wire [31:0] bit_extender_1_out;

  _2_s_Comp__for_MULT u_2_s_comp_for_mult_1 (
    .Input_A(Input_A), .Add(1'b1), .Sign_bit(Input_A[15]),
    .Absolute_value(n2_s_comp_for_mult_1_absolute_value));  // open: c_out
  xor xor_1 (xor_1_out, Input_A[15], Input_B[15]);
  _2_s_Comp__for_MULT u_2_s_comp_for_mult_2 (
    .Input_A(Input_B), .Add(1'b1), .Sign_bit(Input_B[15]),
    .Absolute_value(n2_s_comp_for_mult_2_absolute_value));  // open: c_out
  Multiplier #(.width(16)) multiplier_1 (
    .a(n2_s_comp_for_mult_1_absolute_value), .b(n2_s_comp_for_mult_2_absolute_value), .out(multiplier_1_out),
    .cout(multiplier_1_cout));  // open: cin
  _2_s_Comp__for_MULT u_2_s_comp_for_mult_3 (
    .Input_A(multiplier_1_cout), .Add(n2_s_comp_for_mult_4_c_out), .Sign_bit(xor_1_out), .Absolute_value(R13));  // open: c_out
  assign bit_extender_1_out = {{16{Main_result[15]}}, Main_result[15:0]};  // Bit_Extender bit_extender_1
  _2_s_Comp__for_MULT u_2_s_comp_for_mult_4 (
    .Input_A(multiplier_1_out), .Add(1'b1), .Sign_bit(xor_1_out), .Absolute_value(Main_result[15:0]),
    .c_out(n2_s_comp_for_mult_4_c_out));
  and and_1 (Main_result[16], xor_1_out, ~Main_result[17]);  // AND_Gate
  Comparator #(.width(32)) comparator_1 (
    .a({R13, Main_result[15:0]}), .b({32{1'b0}}), .eq(Main_result[17]));  // open: gt, lt
  not not_1 (Main_result[18], comparator_2_eq);
  Comparator #(.width(32)) comparator_2 (
    .a({R13, Main_result[15:0]}), .b(bit_extender_1_out), .eq(comparator_2_eq));  // open: gt, lt
endmodule

module SETLO (
  input  [7:0] v__b7_0,
  output [20:0] OUTPUT
);

  assign OUTPUT[15:0] = {{8{v__b7_0[7]}}, v__b7_0};  // Bit_Extender bit_extender_1
endmodule

module SETHI (
  input  [15:0] Input_A__Rd,
  input  [7:0] v__b7_0,
  output [20:0] OUTPUT
);


  assign OUTPUT[15:0] = {v__b7_0, Input_A__Rd[7:0]};
endmodule

// inv
module _2_s_Comp__for_MULT (
  input  [15:0] Input_A,
  input  Add,
  input  Sign_bit,
  output [15:0] Absolute_value,
  output c_out
);

  wire [15:0] adder_1_out, bit_extender_1_out, not_1_out;

  not not_1 (not_1_out[0], Input_A[0]);
  not not_2 (not_1_out[1], Input_A[1]);
  not not_3 (not_1_out[2], Input_A[2]);
  not not_4 (not_1_out[3], Input_A[3]);
  not not_5 (not_1_out[4], Input_A[4]);
  not not_6 (not_1_out[5], Input_A[5]);
  not not_7 (not_1_out[6], Input_A[6]);
  not not_8 (not_1_out[7], Input_A[7]);
  not not_9 (not_1_out[8], Input_A[8]);
  not not_10 (not_1_out[9], Input_A[9]);
  not not_11 (not_1_out[10], Input_A[10]);
  not not_12 (not_1_out[11], Input_A[11]);
  not not_13 (not_1_out[12], Input_A[12]);
  not not_14 (not_1_out[13], Input_A[13]);
  not not_15 (not_1_out[14], Input_A[14]);
  not not_16 (not_1_out[15], Input_A[15]);
  assign bit_extender_1_out = {{15{1'b0}}, Add};  // Bit_Extender bit_extender_1
  Adder #(.width(16)) adder_1 (.a(not_1_out), .b(bit_extender_1_out), .out(adder_1_out), .cout(c_out));  // open: cin
  Multiplexer #(.width(16)) multiplexer_1 (
    .in0(Input_A), .in1(adder_1_out), .out(Absolute_value), .sel(Sign_bit));  // open: en
endmodule

// Misc
module Miscellaneous__rselectA_MULT (
  input  [15:0] Instruction,
  output enable_Rt,
  output [3:0] rselectA
);

  wire decoder_1_out3, decoder_1_out6, decoder_1_out7, decoder_1_out15, or_1_out;

  Comparator #(.width(4)) comparator_1 (.a(Instruction[15:12]), .b(4'b1100), .eq(enable_Rt));  // open: gt, lt
  Decoder #(.select(4)) decoder_1 (
    .out3(decoder_1_out3), .out6(decoder_1_out6), .out7(decoder_1_out7), .out15(decoder_1_out15),
    .sel(Instruction[15:12]));  // open: out0, out1, out2, out4, out5, out8, out9, out10, out11, out12, out13, out14, en
  or or_1 (or_1_out, decoder_1_out15, decoder_1_out7, decoder_1_out6, decoder_1_out3);
  Multiplexer #(.width(4)) multiplexer_1 (
    .in0(Instruction[7:4]), .in1(Instruction[11:8]), .out(rselectA), .sel(or_1_out));  // open: en
endmodule

// T1
module Write_Enable (
  input  [15:0] Instruction,
  output WriteEnable_YYT1
);

  wire bitselector_1_out;

  BitSelector bitselector_1 (.in(Instruction[7:0]), .out(bitselector_1_out), .sel(3'b000));
  and and_1 (WriteEnable_YYT1, Instruction[15], ~Instruction[14], Instruction[13], ~Instruction[12], ~Instruction[11], ~Instruction[10], ~Instruction[9], ~Instruction[8], bitselector_1_out);  // AND_Gate
endmodule

module key0 (
  input  in_1,
  input  [15:0] Instruction,
  output KeyBoardEnable_YYT1
);

  wire and_2_out, bitselector_1_out;

  BitSelector bitselector_1 (.in(Instruction[7:0]), .out(bitselector_1_out), .sel(3'b000));
  and and_1 (KeyBoardEnable_YYT1, in_1, and_2_out);
  and and_2 (and_2_out, ~Instruction[15], ~Instruction[14], Instruction[13], ~Instruction[12], Instruction[11], ~Instruction[10], Instruction[9], ~Instruction[8], ~bitselector_1_out);  // AND_Gate
endmodule

module key2 (
  input  in_1,
  input  [15:0] Instruction,
  output KeyBoardEnable_YYT1
);

  wire and_2_out, bitselector_1_out;

  BitSelector bitselector_1 (.in(Instruction[7:0]), .out(bitselector_1_out), .sel(3'b000));
  and and_1 (KeyBoardEnable_YYT1, in_1, and_2_out);
  and and_2 (and_2_out, ~Instruction[15], ~Instruction[14], Instruction[13], ~Instruction[12], Instruction[11], ~Instruction[10], Instruction[9], ~Instruction[8], bitselector_1_out);  // AND_Gate
endmodule

// T2
module enable_t2 (
  input  [15:0] Instruction,
  output WriteEnable_YYt2
);

  wire bitselector_1_out;

  BitSelector bitselector_1 (.in(Instruction[7:0]), .out(bitselector_1_out), .sel(3'b000));
  and and_1 (WriteEnable_YYt2, Instruction[15], ~Instruction[14], Instruction[13], ~Instruction[12], ~Instruction[11], ~Instruction[10], ~Instruction[9], ~Instruction[8], ~bitselector_1_out);  // AND_Gate
endmodule

// HWI
module Hardware_Interrupt (
  input  clock,
  input  [15:0] Instruction,
  input  key_in_board,
  input  [15:0] Input_A,
  input  [15:0] PC,
  input  [3:0] WHich_interupt,
  output toggle_interupt,
  output [15:0] FP__w,
  output [15:0] PC__w
);

  wire and_1_out, comparator_1_eq, not_1_out, not_2_out, register_2_q;
  wire [15:0] multiplexer_1_out, register_1_q;

  Comparator #(.width(16), .mode("unsigned")) comparator_1 (
    .a(Instruction), .b(16'h2300), .eq(comparator_1_eq));  // open: gt, lt
  Multiplexer #(.select(4), .width(16), .enable("false")) multiplexer_1 (
    .in1(16'hbbb0), .in2(16'hbc00), .out(multiplexer_1_out), .sel(WHich_interupt));  // open: in0, in3, in4, in5, in6, in7, in8, in9, in10, in11, in12, in13, in14, in15
  Register #(.width(16)) register_1 (.D(PC), .en(and_1_out), .Q(register_1_q), .clk(clock));  // open: clr
  Register #(.width(1)) register_2 (
    .D(key_in_board), .en(and_1_out), .Q(register_2_q), .clk(clock), .clr(comparator_1_eq));
  not not_1 (not_1_out, register_2_q);
  and and_1 (and_1_out, key_in_board, not_1_out);
  Multiplexer #(.width(16)) multiplexer_2 (.in1(Input_A), .out(FP__w), .sel(and_1_out));  // open: in0, en
  or or_1 (toggle_interupt, comparator_1_eq, and_1_out);
  not not_2 (not_2_out, comparator_1_eq);
  Multiplexer #(.width(16)) multiplexer_3 (
    .in0(register_1_q), .in1(multiplexer_1_out), .out(PC__w), .sel(not_2_out));  // open: en
endmodule

module PC_Ctrl (
  input  [15:0] PC_Branch,
  input  [15:0] PC_C_R,
  input  [15:0] PC_Int,
  input  [15:0] PC_SWI,
  input  Branch,
  input  Call,
  input  HW_Interrupt,
  input  SW_Int,
  input  CLK,
  output [15:0] PC_out,
  output PC_Change
);

  wire comparator_1_eq;
  wire [7:0] counter_1_q;
  wire [15:0] multiplexer_1_out;

  Counter counter_1 (.D(counter_1_q), .Q(counter_1_q), .clk(CLK), .clr(SW_Int));  // open: load, count, carry
  Comparator #(.mode("unsigned")) comparator_1 (.a(counter_1_q), .b(8'h3e), .eq(comparator_1_eq));  // open: gt, lt
  Multiplexer #(.select(4), .width(16)) multiplexer_1 (
    .in1(PC_SWI), .in2(PC_Branch), .in3(PC_SWI), .in4(PC_C_R), .in5(PC_SWI), .in7(PC_SWI), .in8(PC_Int),
    .in9(PC_Int), .in10(PC_Int), .in11(PC_Int), .in12(PC_Int), .in13(PC_Int), .in14(PC_Int), .in15(PC_Int),
    .out(multiplexer_1_out), .sel({HW_Interrupt, Call, Branch, SW_Int}));  // open: in0, in6, en
  Multiplexer #(.width(16)) multiplexer_2 (
    .in0(multiplexer_1_out), .in1(16'hffa0), .out(PC_out), .sel(comparator_1_eq));  // open: en
  or or_1 (PC_Change, HW_Interrupt, Call, comparator_1_eq, Branch, SW_Int);
endmodule

module which_int (
  input  in_1,
  input  in_2,
  output out_3,
  output [3:0] out_4
);

  wire and_1_out;

  or or_1 (out_3, in_1, in_2);
  and and_1 (and_1_out, ~in_1, in_2);  // AND_Gate
  Multiplexer #(.width(4)) multiplexer_1 (.in0(4'b0001), .in1(4'b0010), .out(out_4), .sel(and_1_out));  // open: en
endmodule

// SWI
module Software_Interrupt (
  input  clock,
  input  [15:0] Instruction,
  input  [15:0] Input_A,
  input  [15:0] PC,
  output toggle_interupt,
  output [15:0] FP__w,
  output [15:0] PC__w
);

  wire and_1_out, comparator_1_gt, comparator_2_lt, comparator_3_eq, not_1_out;
  wire [15:0] adder_1_out, multiplexer_1_out, register_1_q;

  Comparator #(.width(16), .mode("unsigned")) comparator_1 (
    .a(Instruction), .b(16'h2200), .gt(comparator_1_gt));  // open: eq, lt
  Comparator #(.width(16), .mode("unsigned")) comparator_2 (
    .a(Instruction), .b(16'h2210), .lt(comparator_2_lt));  // open: gt, eq
  Comparator #(.width(16), .mode("unsigned")) comparator_3 (
    .a(Instruction), .b(16'h2300), .eq(comparator_3_eq));  // open: gt, lt
  Multiplexer #(.select(4), .width(16), .enable("false")) multiplexer_1 (
    .in1(16'h8000), .in2(16'h9000), .in3(16'ha000), .in4(16'hb000), .in5(16'hc000), .in6(16'hd000),
    .in7(16'he000), .in8(16'hf000), .out(multiplexer_1_out), .sel(Instruction[3:0]));  // open: in0, in9, in10, in11, in12, in13, in14, in15
  and and_1 (and_1_out, comparator_1_gt, comparator_2_lt);
  Register #(.width(16)) register_1 (.D(PC), .en(and_1_out), .Q(register_1_q), .clk(clock));  // open: clr
  Adder #(.width(16)) adder_1 (.a(register_1_q), .b(16'h1), .out(adder_1_out));  // open: cin, cout
  Multiplexer #(.width(16)) multiplexer_2 (.in1(Input_A), .out(FP__w), .sel(and_1_out));  // open: in0, en
  not not_1 (not_1_out, comparator_3_eq);
  Multiplexer #(.width(16)) multiplexer_3 (
    .in0(adder_1_out), .in1(multiplexer_1_out), .out(PC__w), .sel(not_1_out));  // open: en
  or or_1 (toggle_interupt, comparator_3_eq, and_1_out);
endmodule
